# Fritzing sketch Untitled Sketch (saved by Fritzing 0.9.3b)
breadboards: 1

parts:
  Parça1 = Arduino Uno (Rev3)
  Parça2 = RFID-RC522-v2
  LED1 = LED - 5mm [color="Red (633nm)" package="5 mm [THT]"]
  R1 = Resistor [tolerance=±5% resistance=330 package=THT]
  VCC1 = Battery  # not connected

nets:
  N1: Parça1.D8, R1.Pin_0
  N2: Parça1.D9_PWM, Parça2.RST
  N3: Parça1.D10_PWM/SS, Parça2.SDA
  N4: Parça1.D11_PWM/MOSI, Parça2.MOSI
  N5: Parça1.D12/MISO, Parça2.MISO
  N6: Parça1.D13/SCK, Parça2.SCK
  3V3: Parça1.3V3, Parça2.3.3V
  GND: Parça1.GND, Parça2.GND, LED1.anode
  N7: LED1.cathode, R1.Pin_1

custom parts:
  RFID-RC522-v2: A simple China made RFID-RC522 Reader; do check the pin labels, as this is a MFRC522 based clone.

// code stored in the sketch: Untitled.ino
#include <SPI.h>
#include <MFRC522.h>
 
#define SS_PIN 10
#define RST_PIN 9
MFRC522 mfrc522(SS_PIN, RST_PIN);  
 
void setup() 
{
  Serial.begin(9600);   
  SPI.begin();      
  mfrc522.PCD_Init();  
  Serial.println("KARTINI OKUT");
  Serial.println();
  pinMode(8,OUTPUT);
  pinMode(2,OUTPUT);
  pinMode(3,OUTPUT);
  pinMode(4,OUTPUT);
}
void loop() 
{
  // Look for new cards
  if ( ! mfrc522.PICC_IsNewCardPresent()) 
  {
    return;
  }
  // Select one of the cards
  if ( ! mfrc522.PICC_ReadCardSerial()) 
  {
    return;
  }
  //Show UID on serial monitor
  Serial.print("UID ET?KET?:");
  String content= "";
  byte letter;
  for (byte i = 0; i < mfrc522.uid.size; i++) 
  {
     Serial.print(mfrc522.uid.uidByte[i] < 0x10 ? " 0" : " ");
     Serial.print(mfrc522.uid.uidByte[i], HEX);
     content.concat(String(mfrc522.uid.uidByte[i] < 0x10 ? " 0" : " "));
     content.concat(String(mfrc522.uid.uidByte[i], HEX));
  }
  Serial.println();
  Serial.print("MESAJ : ");
  content.toUpperCase();
  if (content.substring(1) == "A0 5F D5 83") 
  {
    Serial.println("ER???ME ?Z?N VER?LD?");
    Serial.println();
    digitalWrite(8,HIGH);
    delay(1000);
    digitalWrite(8,LOW);
  }
 
 else   {
    Serial.println("ER???M REDDED?LD?");
    delay(3000);
  }
}
